# Fritzing sketch schematic (saved by Fritzing 0.7.0b)

parts:
  Part1 = Arduino Musical Instrument Shield
  Part2 = IMU Analog Combo Board - 5 Degrees of Freedom
  Pololu_Dual_Motor_Driver1 = Pololu_Dual_VNH2SP30_Motor_Driver_Carrier_MD03A
  Netduino1 = Netduino
  J1 = Infrared Proximity Sensor
  J2 = Infrared Proximity Sensor
  M1 = DC Motor [part_number="Pololu 50:1 Metal Gearmotor 37Dx54L mm"]
  M2 = DC Motor [part_number="Pololu 50:1 Metal Gearmotor 37Dx54L mm"]
  K1 = Relay [part_number=FRS1B-S package=THT]

nets:
  N1: Part1.MIDI-IN, Netduino1.D3_TX1
  N2: Part1.MIDI-RESET, Netduino1.D4_CS0
  N3: Part2.XOUT, Netduino1.A0
  N4: Part2.YOUT, Netduino1.A1
  N5: Part2.ZOUT, Netduino1.A2
  N6: Part2.XRATE, Netduino1.A3
  N7: Pololu_Dual_Motor_Driver1.OUT_1A, M1.pin_1
  N8: Pololu_Dual_Motor_Driver1.OUT_1B, M1.pin_2
  N9: Pololu_Dual_Motor_Driver1.VIN+, K1.B
  N10: Pololu_Dual_Motor_Driver1.OUT_2A, M2.pin_1
  N11: Pololu_Dual_Motor_Driver1.OUT_2B, M2.pin_2
  N12: Pololu_Dual_Motor_Driver1.1_INA, Netduino1.D12_MISO
  N13: Pololu_Dual_Motor_Driver1.1_INB, Netduino1.D11_MOSI
  N14: Pololu_Dual_Motor_Driver1.1_PWM, Netduino1.D10_PWM3
  N15: Pololu_Dual_Motor_Driver1.2_PWM, Netduino1.D9_PWM2
  N16: Pololu_Dual_Motor_Driver1.2_INB, Netduino1.D8_CTS1
  N17: Pololu_Dual_Motor_Driver1.2_INA, Netduino1.D7_RTS1
  N18: Netduino1.Aref, Netduino1.+5V
  N19: Netduino1.D13_SPCK, K1.COIL2
  N20: Netduino1.A4_TWD, J2.Vout
  N21: Netduino1.A5_TWCK, J1.Vout

notes:
  WiFi Chip Here. Gets full U1RX/TX
  Receive bytes from Remote (RF). Only uses U2RX on Netduino. U2TX is used for the MIDI shield.
  11.1V Battery Source. Also powers the rest of the electronics but those connections aren't shown in this schematic.
  Relay signal is enable/disable motors. This signal is set to low by the Netduino if it sees a kill signal from the remote.
